// Logisim project halfadder1.circ as structural Verilog: 2 circuits, main circuit main
module main (
  input  in_1,
  input  in_2,
  input  in_3,
  input  in_4,
  output out_5,
  output out_6,
  output out_7,
  output out_8
);

  halfadder halfadder_1 (.A(in_3), .B(in_4), .out_3(out_7), .out_4(out_8));
  xor xor_1 (out_5, in_1, in_2);
  // AND_Gate and_1 has open pins: in1=in_2, out=open
endmodule

module halfadder (
  input  A,
  input  B,
  output out_3,
  output out_4
);

  xor xor_1 (out_3, A, B);
  and and_1 (out_4, A, B);
endmodule
